// Logisim project elementary-gates.circ as structural Verilog: 13 circuits, main circuit Xor
module Xor (
  input  a,
  input  b,
  output out
);

  wire and_1_out, and_2_out, not_1_out, not_2_out;

  not not_1 (not_1_out, a);
  not not_2 (not_2_out, b);
  and and_1 (and_1_out, not_1_out, b);
  and and_2 (and_2_out, a, not_2_out);
  or or_1 (out, and_1_out, and_2_out);

  // Notes on the sheet:
  //   Xor
endmodule

module Multiplexor (
  input  a,
  input  b,
  input  sel,
  output out
);

  wire and_1_out, and_2_out, not_1_out;

  not not_1 (not_1_out, sel);
  and and_1 (and_1_out, a, not_1_out);
  and and_2 (and_2_out, b, sel);
  or or_1 (out, and_1_out, and_2_out);

  // Notes on the sheet:
  //   Multiplexor
endmodule

module Demultiplexor (
  input  In,
  input  sel,
  output A,
  output B
);

  wire not_1_out;

  not not_1 (not_1_out, sel);
  and and_1 (A, In, not_1_out);
  and and_2 (B, In, sel);

  // Notes on the sheet:
  //   Demultiplexor
endmodule

module _16_bit_Not (
  input  [15:0] In,
  output [15:0] Out
);

  assign Out = ~In;  // NOT_Gate not_1, 16 bits wide

  // Notes on the sheet:
  //   16-bit Not
endmodule

module _16_bit_And (
  input  [15:0] a,
  input  [15:0] b,
  output [15:0] out
);

  assign out = a & b;  // AND_Gate and_1, 16 bits wide

  // Notes on the sheet:
  //   16-bit And
endmodule

module _16_bit_Or (
  input  [15:0] a,
  input  [15:0] b,
  output [15:0] out
);

  assign out = a | b;  // OR_Gate or_1, 16 bits wide

  // Notes on the sheet:
  //   16-bit OR
endmodule

module _16_bit_Multiplexor (
  input  [15:0] a,
  input  [15:0] b,
  input  sel,
  output [15:0] out
);

  Multiplexer #(.width(16)) multiplexer_1 (.in0(a), .in1(b), .out(out), .sel(sel));  // open: en
endmodule

module _8_way_Or (
  input  in_1,
  input  in_2,
  input  in_3,
  input  in_4,
  input  in_5,
  input  in_6,
  input  in_7,
  input  in_8,
  output out_9
);

  or or_1 (out_9, in_1, in_2, in_3, in_4, in_5, in_6, in_7, in_8);

  // Notes on the sheet:
  //   8-way Or
endmodule

module _4_way_16_bit_Multiplexor (
  input  [15:0] a,
  input  [15:0] b,
  input  [15:0] c,
  input  [15:0] d,
  input  sel_1,
  input  sel_0,
  output [15:0] out
);

  wire [15:0] n16_bit_multiplexor_1_out, n16_bit_multiplexor_2_out;

  _16_bit_Multiplexor u_16_bit_multiplexor_1 (.a(a), .b(b), .out(n16_bit_multiplexor_1_out), .sel(sel_0));
  _16_bit_Multiplexor u_16_bit_multiplexor_2 (.a(c), .b(d), .out(n16_bit_multiplexor_2_out), .sel(sel_0));
  _16_bit_Multiplexor u_16_bit_multiplexor_3 (
    .a(n16_bit_multiplexor_1_out), .b(n16_bit_multiplexor_2_out), .out(out), .sel(sel_1));

  // Notes on the sheet:
  //   4-way 16-bit Multiplexor
endmodule

module _8_way_16_bit_Multiplexor (
  input  [15:0] a,
  input  [15:0] b,
  input  [15:0] c,
  input  [15:0] d,
  input  [15:0] e,
  input  [15:0] f,
  input  [15:0] g,
  input  [15:0] h,
  input  sel_2,
  input  sel_1,
  input  sel_0,
  output [15:0] out
);

  wire [15:0] n4_way_16_bit_multiplexor_1_out, n4_way_16_bit_multiplexor_2_out;

  _4_way_16_bit_Multiplexor u_4_way_16_bit_multiplexor_1 (
    .a(a), .b(b), .c(c), .d(d), .out(n4_way_16_bit_multiplexor_1_out), .sel_1(sel_1), .sel_0(sel_0));
  _4_way_16_bit_Multiplexor u_4_way_16_bit_multiplexor_2 (
    .a(e), .b(f), .c(g), .d(h), .out(n4_way_16_bit_multiplexor_2_out), .sel_1(sel_1), .sel_0(sel_0));
  _16_bit_Multiplexor u_16_bit_multiplexor_1 (
    .a(n4_way_16_bit_multiplexor_1_out), .b(n4_way_16_bit_multiplexor_2_out), .out(out), .sel(sel_2));

  // Notes on the sheet:
  //   8-way 16-bit Multiplexor
endmodule

module _4_way_1_bit_Demultiplexor (
  input  in,
  input  sel_0,
  input  sel_1,
  output a,
  output b,
  output c,
  output d
);

  wire demultiplexor_1_a, demultiplexor_1_b, demultiplexor_2_a, demultiplexor_2_b, not_1_out;

  Demultiplexor demultiplexor_1 (.In(in), .A(demultiplexor_1_a), .B(demultiplexor_1_b), .sel(sel_0));
  Demultiplexor demultiplexor_2 (.In(in), .A(demultiplexor_2_a), .B(demultiplexor_2_b), .sel(sel_0));
  not not_1 (not_1_out, sel_1);
  and and_1 (a, not_1_out, demultiplexor_1_a);
  and and_2 (b, not_1_out, demultiplexor_1_b);
  and and_3 (c, sel_1, demultiplexor_2_a);
  and and_4 (d, sel_1, demultiplexor_2_b);

  // Notes on the sheet:
  //   4-way 1-bit Demultiplexor
endmodule

module _8_way_1_bit_Demultiplexor (
  input  in,
  input  sel_0,
  input  sel_1,
  input  sel_2,
  output a,
  output b,
  output c,
  output d,
  output e,
  output f,
  output g,
  output h
);

  wire n4_way_1_bit_demultiplexor_1_a, n4_way_1_bit_demultiplexor_1_b, n4_way_1_bit_demultiplexor_1_c,
       n4_way_1_bit_demultiplexor_1_d, n4_way_1_bit_demultiplexor_2_a, n4_way_1_bit_demultiplexor_2_b,
       n4_way_1_bit_demultiplexor_2_c, n4_way_1_bit_demultiplexor_2_d, not_1_out;

  _4_way_1_bit_Demultiplexor u_4_way_1_bit_demultiplexor_1 (
    .in(in), .a(n4_way_1_bit_demultiplexor_1_a), .b(n4_way_1_bit_demultiplexor_1_b),
    .c(n4_way_1_bit_demultiplexor_1_c), .d(n4_way_1_bit_demultiplexor_1_d), .sel_1(sel_1), .sel_0(sel_0));
  _4_way_1_bit_Demultiplexor u_4_way_1_bit_demultiplexor_2 (
    .in(in), .a(n4_way_1_bit_demultiplexor_2_a), .b(n4_way_1_bit_demultiplexor_2_b),
    .c(n4_way_1_bit_demultiplexor_2_c), .d(n4_way_1_bit_demultiplexor_2_d), .sel_1(sel_1), .sel_0(sel_0));
  not not_1 (not_1_out, sel_2);
  and and_1 (a, not_1_out, n4_way_1_bit_demultiplexor_1_a);
  and and_2 (b, not_1_out, n4_way_1_bit_demultiplexor_1_b);
  and and_3 (c, not_1_out, n4_way_1_bit_demultiplexor_1_c);
  and and_4 (d, not_1_out, n4_way_1_bit_demultiplexor_1_d);
  and and_5 (e, sel_2, n4_way_1_bit_demultiplexor_2_a);
  and and_6 (f, sel_2, n4_way_1_bit_demultiplexor_2_b);
  and and_7 (g, sel_2, n4_way_1_bit_demultiplexor_2_c);
  and and_8 (h, sel_2, n4_way_1_bit_demultiplexor_2_d);

  // Notes on the sheet:
  //   8-way 1-bit Demultiplexor
endmodule

module main (
  input  in_1,
  input  in_2,
  input  in_3,
  input  in_4,
  input  in_5,
  input  in_6,
  input  in_7,
  output out_8,
  output out_9,
  output out_10,
  output out_11,
  output out_12
);

  _8_way_1_bit_Demultiplexor u_8_way_1_bit_demultiplexor_1 (
    .in(in_2), .a(out_8), .b(out_9), .c(out_10), .d(out_12), .sel_2(in_7), .sel_1(in_6), .sel_0(in_5));  // open: e, f, g, h
  Multiplexor multiplexor_1 (.a(in_1), .b(in_3), .out(out_11), .sel(in_4));

  // Notes on the sheet:
  //   Tip: use this subcircuit to test the library's chips.
endmodule
