// Logisim project alu.circ as structural Verilog: 7 circuits, main circuit main
module main (
  input  in_1,
  input  in_2,
  input  [15:0] in_3,
  input  in_4,
  input  in_5,
  input  in_6,
  input  in_7,
  input  in_8,
  input  in_9,
  input  in_10,
  input  [15:0] in_11,
  input  [15:0] in_12,
  input  [15:0] in_13,
  input  [15:0] in_14,
  output out_15,
  output [15:0] out_16,
  output out_17,
  output [15:0] out_18,
  output [15:0] out_19,
  output out_20,
  output out_21
);

  Full_Adder full_adder_1 (.a(in_1), .b(in_2), .carry_in(in_4), .sum(out_15), .carry_out(out_17));
  _16_bit_Adder u_16_bit_adder_1 (.in_1(in_11), .in_2(in_13), .out_3(out_18));
  _16_bit_Incrementer u_16_bit_incrementer_1 (.in_1(in_3), .out_2(out_16));
  ALU alu_1 (
    .in_7(in_12), .in_8(in_14), .out(out_19), .ZX(in_5), .NX(in_6), .ZY(in_7), .NY(in_8), .F(in_9),
    .NO(in_10), .NG(out_21), .ZR(out_20));

  // Notes on the sheet:
  //   a
  //   b
  //   Tip: use this subcircuit to test the library's chips.
  //   a
  //   b
endmodule

module ALU (
  input  ZX,
  input  NX,
  input  ZY,
  input  NY,
  input  F,
  input  NO,
  input  [15:0] in_7,
  input  [15:0] in_8,
  output [15:0] out,
  output NG,
  output ZR
);

  wire n8_way_or_1_out_9, n8_way_or_2_out_9, or_1_out;
  wire [15:0] n16_bit_adder_1_out_3, n16_bit_and_1_out, n16_bit_multiplexor_1_out, n16_bit_multiplexor_2_out,
       n16_bit_multiplexor_3_out, n16_bit_multiplexor_4_out, n16_bit_multiplexor_5_out, n16_bit_not_1_out,
       n16_bit_not_2_out, n16_bit_not_3_out;

  _16_bit_Multiplexor u_16_bit_multiplexor_1 (.a(in_7), .b({16{1'b0}}), .out(n16_bit_multiplexor_1_out), .sel(ZX));
  _16_bit_Multiplexor u_16_bit_multiplexor_2 (.a(in_8), .b({16{1'b0}}), .out(n16_bit_multiplexor_2_out), .sel(ZY));
  _16_bit_Not u_16_bit_not_1 (.In(n16_bit_multiplexor_1_out), .Out(n16_bit_not_1_out));
  _16_bit_Not u_16_bit_not_2 (.In(n16_bit_multiplexor_2_out), .Out(n16_bit_not_2_out));
  _16_bit_Multiplexor u_16_bit_multiplexor_3 (
    .a(n16_bit_multiplexor_1_out), .b(n16_bit_not_1_out), .out(n16_bit_multiplexor_3_out), .sel(NX));
  _16_bit_Multiplexor u_16_bit_multiplexor_4 (
    .a(n16_bit_multiplexor_2_out), .b(n16_bit_not_2_out), .out(n16_bit_multiplexor_4_out), .sel(NY));
  _16_bit_And u_16_bit_and_1 (.a(n16_bit_multiplexor_3_out), .b(n16_bit_multiplexor_4_out), .out(n16_bit_and_1_out));
  _16_bit_Adder u_16_bit_adder_1 (
    .in_1(n16_bit_multiplexor_3_out), .in_2(n16_bit_multiplexor_4_out), .out_3(n16_bit_adder_1_out_3));
  _16_bit_Multiplexor u_16_bit_multiplexor_5 (
    .a(n16_bit_and_1_out), .b(n16_bit_adder_1_out_3), .out(n16_bit_multiplexor_5_out), .sel(F));
  _16_bit_Not u_16_bit_not_3 (.In(n16_bit_multiplexor_5_out), .Out(n16_bit_not_3_out));
  _16_bit_Multiplexor u_16_bit_multiplexor_6 (
    .a(n16_bit_multiplexor_5_out), .b(n16_bit_not_3_out), .out({NG, out[14:0]}), .sel(NO));
  _8_way_Or u_8_way_or_1 (
    .in_1(out[8]), .in_2(out[9]), .in_3(out[10]), .in_4(out[11]), .in_5(out[12]), .in_6(out[13]),
    .in_7(out[14]), .in_8(NG), .out_9(n8_way_or_1_out_9));
  or or_1 (or_1_out, n8_way_or_1_out_9, n8_way_or_2_out_9);
  not not_1 (ZR, or_1_out);
  _8_way_Or u_8_way_or_2 (
    .in_1(out[0]), .in_2(out[1]), .in_3(out[2]), .in_4(out[3]), .in_5(out[4]), .in_6(out[5]), .in_7(out[6]),
    .in_8(out[7]), .out_9(n8_way_or_2_out_9));

  assign out[15] = NG;

  // Notes on the sheet:
  //   a
  //   b
endmodule

module Full_Adder (
  input  a,
  input  b,
  input  carry_in,
  output sum,
  output carry_out
);

  wire and_1_out, and_2_out, xor_1_out;

  xor xor_1 (xor_1_out, a, b);
  and and_1 (and_1_out, b, a);
  xor xor_2 (sum, xor_1_out, carry_in);
  and and_2 (and_2_out, carry_in, xor_1_out);
  or or_1 (carry_out, and_2_out, and_1_out);

  // Notes on the sheet:
  //   Full-Adder
endmodule

module Half_Adder (
  input  a,
  input  b,
  output sum,
  output carry
);

  xor xor_1 (sum, a, b);
  and and_1 (carry, b, a);

  // Notes on the sheet:
  //   Half-Adder
endmodule

module _4_bit_Adder (
  input  [3:0] a,
  input  [3:0] b,
  input  carry_in,
  output [3:0] out,
  output carry_out
);

  wire full_adder_1_carry_out, full_adder_2_carry_out, full_adder_3_carry_out;

  Full_Adder full_adder_1 (.a(a[0]), .b(b[0]), .carry_in(carry_in), .sum(out[0]), .carry_out(full_adder_1_carry_out));
  Full_Adder full_adder_2 (
    .a(a[1]), .b(b[1]), .carry_in(full_adder_1_carry_out), .sum(out[1]), .carry_out(full_adder_2_carry_out));
  Full_Adder full_adder_3 (
    .a(a[2]), .b(b[2]), .carry_in(full_adder_2_carry_out), .sum(out[2]), .carry_out(full_adder_3_carry_out));
  Full_Adder full_adder_4 (.a(a[3]), .b(b[3]), .carry_in(full_adder_3_carry_out), .sum(out[3]), .carry_out(carry_out));

  // Notes on the sheet:
  //   0
  //   0
  //   +
  //   1
  //   0
  //   0
  //   1010
  //   0011
  //   -------------------
  //   1101
  //   4-bit Adder
endmodule

module _16_bit_Adder (
  input  [15:0] in_1,
  input  [15:0] in_2,
  output [15:0] out_3
);

  wire n4_bit_adder_1_carry_out, n4_bit_adder_2_carry_out, n4_bit_adder_3_carry_out;

  _4_bit_Adder u_4_bit_adder_1 (
    .carry_in(1'b0), .a(in_1[3:0]), .b(in_2[3:0]), .out(out_3[3:0]), .carry_out(n4_bit_adder_1_carry_out));
  _4_bit_Adder u_4_bit_adder_2 (
    .carry_in(n4_bit_adder_1_carry_out), .a(in_1[7:4]), .b(in_2[7:4]), .out(out_3[7:4]),
    .carry_out(n4_bit_adder_2_carry_out));
  _4_bit_Adder u_4_bit_adder_3 (
    .carry_in(n4_bit_adder_2_carry_out), .a(in_1[11:8]), .b(in_2[11:8]), .out(out_3[11:8]),
    .carry_out(n4_bit_adder_3_carry_out));
  _4_bit_Adder u_4_bit_adder_4 (
    .carry_in(n4_bit_adder_3_carry_out), .a(in_1[15:12]), .b(in_2[15:12]), .out(out_3[15:12]));  // open: carry_out

  // Notes on the sheet:
  //   a
  //   b
  //   out
endmodule

module _16_bit_Incrementer (
  input  [15:0] in_1,
  output [15:0] out_2
);

  _16_bit_Adder u_16_bit_adder_1 (.in_1(in_1), .in_2(16'h1), .out_3(out_2));
endmodule
