// Logisim project hack-computer.circ as structural Verilog: 3 circuits, main circuit Hack Computer
module CPU (
  input  [15:0] Instruction,
  input  [15:0] InM,
  input  Reset,
  output [15:0] OutM,
  output WriteM,
  output [5:0] AddressM,
  output [5:0] PC
);

  wire alu_1_ng, alu_1_zr, and_1_out, and_2_out, and_3_out, and_4_out, and_5_out, and_6_out,
       multiplexor_1_out, multiplexor_2_out, multiplexor_3_out, not_1_out, not_2_out, or_1_out;
  wire [15:0] n16_bit_multiplexor_1_out, n16_bit_multiplexor_2_out, n16_bit_register_2_out_3;
  wire [15:6] n16_bit_register_1_out_3, program_counter_1_out_5;

  _16_bit_Multiplexor u_16_bit_multiplexor_1 (
    .a(Instruction), .b(OutM), .out(n16_bit_multiplexor_1_out), .sel(Instruction[15]));
  Multiplexor multiplexor_1 (.a(1'b1), .b(Instruction[5]), .out(multiplexor_1_out), .sel(Instruction[15]));
  _16_bit_Register u_16_bit_register_1 (
    .in_2(n16_bit_multiplexor_1_out), .out_3({n16_bit_register_1_out_3, AddressM}), .in_1(multiplexor_1_out));
  Clock clock_1 ();  // open: out
  Multiplexor multiplexor_2 (.a(1'b0), .b(Instruction[4]), .out(multiplexor_2_out), .sel(Instruction[15]));
  Multiplexor multiplexor_3 (.a(1'b0), .b(or_1_out), .out(multiplexor_3_out), .sel(Instruction[15]));
  Program_Counter program_counter_1 (
    .In({n16_bit_register_1_out_3, AddressM}), .out_5({program_counter_1_out_5, PC}), .in_1(1'b1),
    .in_2(multiplexor_3_out), .in_3(Reset));
  _16_bit_Register u_16_bit_register_2 (.in_2(OutM), .out_3(n16_bit_register_2_out_3), .in_1(multiplexor_2_out));
  _16_bit_Multiplexor u_16_bit_multiplexor_2 (
    .a({n16_bit_register_1_out_3, AddressM}), .b(InM), .out(n16_bit_multiplexor_2_out), .sel(Instruction[12]));
  or or_1 (or_1_out, and_2_out, and_4_out, and_6_out);
  ALU alu_1 (
    .in_7(n16_bit_register_2_out_3), .in_8(n16_bit_multiplexor_2_out), .out(OutM), .ZX(Instruction[11]),
    .NX(Instruction[10]), .ZY(Instruction[9]), .NY(Instruction[8]), .F(Instruction[7]), .NO(Instruction[6]),
    .NG(alu_1_ng), .ZR(alu_1_zr));
  not not_1 (not_1_out, alu_1_zr);
  and and_1 (and_1_out, not_1_out, not_2_out);
  and and_2 (and_2_out, Instruction[0], and_1_out);
  not not_2 (not_2_out, alu_1_ng);
  and and_3 (and_3_out, not_2_out, alu_1_zr);
  and and_4 (and_4_out, Instruction[1], and_3_out);
  and and_5 (and_5_out, not_1_out, alu_1_ng);
  and and_6 (and_6_out, Instruction[2], and_5_out);
  Multiplexor multiplexor_4 (.a(1'b0), .b(Instruction[3]), .out(WriteM), .sel(Instruction[15]));

  // Notes on the sheet:
  //   A-Register
  //   Hack Central Processing Unit
  //   D-Register
endmodule

module Hack_Computer (
  input  in_1
);

  wire cpu_1_writem;
  wire [5:0] cpu_1_addressm, cpu_1_pc;
  wire [15:0] cpu_1_outm, ram64_1_out, rom_1_data;

  ROM #(.addrWidth(6), .dataWidth(16)) rom_1 (.addr(cpu_1_pc), .data(rom_1_data));  // open: sel
  CPU cpu_1 (
    .Instruction(rom_1_data), .InM(ram64_1_out), .Reset(in_1), .OutM(cpu_1_outm), .WriteM(cpu_1_writem),
    .AddressM(cpu_1_addressm), .PC(cpu_1_pc));
  Clock clock_1 ();  // open: out
  RAM64 ram64_1 (.In(cpu_1_outm), .Address(cpu_1_addressm), .out(ram64_1_out), .load(cpu_1_writem));

  // Notes on the sheet:
  //   000A
  //   EC10
  //   0005
  //   E308
  //   0004
  //   EA87
  //   Obs: load this into the ROM chip.
  //   Test program - Loading value 10 into RAM's 6th register:
  //   ROM
  //   contents of rom_1 (hex, n*v repeats v):
  //   a ec10 5 e308 4 ea87
  //   HACK COMPUTER
endmodule

module main (
  input  in_1
);

  Hack_Computer hack_computer_1 (.in_1(in_1));

  // Notes on the sheet:
  //   This computer architecture and organization is deeply described in "The Elements of Computing Systems: Building a Modern Computer from First Principles". 
endmodule
