// Logisim project memory-units.circ as structural Verilog: 7 circuits, main circuit main
module main (
  input  in_1,
  input  in_2,
  input  [15:0] in_3,
  input  in_4,
  input  in_5,
  input  in_6,
  input  [5:0] in_7,
  input  in_8,
  input  in_9,
  input  [15:0] in_10,
  input  [3:0] in_11,
  input  [5:0] in_12,
  input  in_13,
  input  in_14,
  input  in_15,
  input  [15:0] in_16,
  output out_17,
  output [15:0] out_18,
  output [15:0] out_19,
  output [3:0] out_20,
  output [15:0] out_21,
  output [15:0] out_22
);

  wire clock_1_out;

  Clock clock_1 (.out(clock_1_out));
  D_Flip_Flop d_ff_1 (.clk(clock_1_out), .D(in_2), .Q(out_17), .preset(in_4), .en(in_6), .reset(in_5));  // open: Qn
  _4_bit_Register u_4_bit_register_1 (.in_2(in_11), .out_3(out_20), .in_1(in_9));
  Clock clock_2 ();  // open: out
  Program_Counter program_counter_1 (.In(in_16), .out_5(out_22), .in_1(in_13), .in_2(in_14), .in_3(in_15));
  _16_bit_Register u_16_bit_register_1 (.in_2(in_3), .out_3(out_18), .in_1(in_1));
  RAM64 ram64_1 (.In(in_10), .Address(in_12), .out(out_21), .load(in_8));
  ROM64 rom64_1 (.Address(in_7), .out(out_19));
endmodule

module _4_bit_Register (
  input  in_1,
  input  [3:0] in_2,
  output [3:0] out_3
);

  wire clock_1_out;

  Clock clock_1 (.out(clock_1_out));
  D_Flip_Flop d_ff_1 (.clk(clock_1_out), .D(in_2[0]), .Q(out_3[0]), .en(in_1));  // open: Qn, preset, reset
  D_Flip_Flop d_ff_2 (.clk(clock_1_out), .D(in_2[1]), .Q(out_3[1]), .en(in_1));  // open: Qn, preset, reset
  D_Flip_Flop d_ff_3 (.clk(clock_1_out), .D(in_2[2]), .Q(out_3[2]), .en(in_1));  // open: Qn, preset, reset
  D_Flip_Flop d_ff_4 (.clk(clock_1_out), .D(in_2[3]), .Q(out_3[3]), .en(in_1));  // open: Qn, preset, reset
endmodule

module _16_bit_Register (
  input  in_1,
  input  [15:0] in_2,
  output [15:0] out_3
);

  Clock clock_1 ();  // open: out
  _4_bit_Register u_4_bit_register_1 (.in_2(in_2[3:0]), .out_3(out_3[3:0]), .in_1(in_1));
  _4_bit_Register u_4_bit_register_2 (.in_2(in_2[7:4]), .out_3(out_3[7:4]), .in_1(in_1));
  _4_bit_Register u_4_bit_register_3 (.in_2(in_2[11:8]), .out_3(out_3[11:8]), .in_1(in_1));
  _4_bit_Register u_4_bit_register_4 (.in_2(in_2[15:12]), .out_3(out_3[15:12]), .in_1(in_1));
endmodule

module RAM64 (
  input  load,
  input  [15:0] In,
  input  [5:0] Address,
  output [15:0] out
);

  wire n8_way_1_bit_demultiplexor_1_a, n8_way_1_bit_demultiplexor_1_b, n8_way_1_bit_demultiplexor_1_c,
       n8_way_1_bit_demultiplexor_1_d, n8_way_1_bit_demultiplexor_1_e, n8_way_1_bit_demultiplexor_1_f,
       n8_way_1_bit_demultiplexor_1_g, n8_way_1_bit_demultiplexor_1_h;
  wire [15:0] ram8_1_out, ram8_2_out, ram8_3_out, ram8_4_out, ram8_5_out, ram8_6_out, ram8_7_out, ram8_8_out;

  _8_way_1_bit_Demultiplexor u_8_way_1_bit_demultiplexor_1 (
    .in(load), .a(n8_way_1_bit_demultiplexor_1_a), .b(n8_way_1_bit_demultiplexor_1_b),
    .c(n8_way_1_bit_demultiplexor_1_c), .d(n8_way_1_bit_demultiplexor_1_d),
    .e(n8_way_1_bit_demultiplexor_1_e), .f(n8_way_1_bit_demultiplexor_1_f),
    .g(n8_way_1_bit_demultiplexor_1_g), .h(n8_way_1_bit_demultiplexor_1_h), .sel_2(Address[5]),
    .sel_1(Address[4]), .sel_0(Address[3]));
  Clock clock_1 ();  // open: out
  RAM8 ram8_1 (.In(In), .Address(Address[2:0]), .out(ram8_1_out), .load(n8_way_1_bit_demultiplexor_1_a));
  RAM8 ram8_2 (.In(In), .Address(Address[2:0]), .out(ram8_2_out), .load(n8_way_1_bit_demultiplexor_1_b));
  RAM8 ram8_3 (.In(In), .Address(Address[2:0]), .out(ram8_3_out), .load(n8_way_1_bit_demultiplexor_1_c));
  RAM8 ram8_4 (.In(In), .Address(Address[2:0]), .out(ram8_4_out), .load(n8_way_1_bit_demultiplexor_1_d));
  RAM8 ram8_5 (.In(In), .Address(Address[2:0]), .out(ram8_5_out), .load(n8_way_1_bit_demultiplexor_1_e));
  RAM8 ram8_6 (.In(In), .Address(Address[2:0]), .out(ram8_6_out), .load(n8_way_1_bit_demultiplexor_1_f));
  RAM8 ram8_7 (.In(In), .Address(Address[2:0]), .out(ram8_7_out), .load(n8_way_1_bit_demultiplexor_1_g));
  RAM8 ram8_8 (.In(In), .Address(Address[2:0]), .out(ram8_8_out), .load(n8_way_1_bit_demultiplexor_1_h));
  _8_way_16_bit_Multiplexor u_8_way_16_bit_multiplexor_1 (
    .a(ram8_1_out), .b(ram8_2_out), .c(ram8_3_out), .d(ram8_4_out), .e(ram8_5_out), .f(ram8_6_out),
    .g(ram8_7_out), .h(ram8_8_out), .out(out), .sel_2(Address[5]), .sel_1(Address[4]), .sel_0(Address[3]));

  // Notes on the sheet:
  //   128-Byte RAM
  //   *Contains 64 16-bit Registers
endmodule

module Program_Counter (
  input  in_1,
  input  in_2,
  input  in_3,
  input  [15:0] In,
  output [15:0] out_5
);

  wire [15:0] n16_bit_incrementer_1_out_2, n16_bit_multiplexor_1_out, n16_bit_multiplexor_2_out,
       n16_bit_multiplexor_3_out;

  _16_bit_Incrementer u_16_bit_incrementer_1 (.in_1(out_5), .out_2(n16_bit_incrementer_1_out_2));
  _16_bit_Multiplexor u_16_bit_multiplexor_1 (
    .a(out_5), .b(n16_bit_incrementer_1_out_2), .out(n16_bit_multiplexor_1_out), .sel(in_1));
  _16_bit_Multiplexor u_16_bit_multiplexor_2 (
    .a(n16_bit_multiplexor_1_out), .b(In), .out(n16_bit_multiplexor_2_out), .sel(in_2));
  Clock clock_1 ();  // open: out
  _16_bit_Multiplexor u_16_bit_multiplexor_3 (
    .a(n16_bit_multiplexor_2_out), .b({16{1'b0}}), .out(n16_bit_multiplexor_3_out), .sel(in_3));
  _16_bit_Register u_16_bit_register_1 (.in_2(n16_bit_multiplexor_3_out), .out_3(out_5), .in_1(1'b1));

  // Notes on the sheet:
  //   16-bit Program Counter
endmodule

module RAM8 (
  input  load,
  input  [15:0] In,
  input  [2:0] Address,
  output [15:0] out
);

  wire n8_way_1_bit_demultiplexor_1_a, n8_way_1_bit_demultiplexor_1_b, n8_way_1_bit_demultiplexor_1_c,
       n8_way_1_bit_demultiplexor_1_d, n8_way_1_bit_demultiplexor_1_e, n8_way_1_bit_demultiplexor_1_f,
       n8_way_1_bit_demultiplexor_1_g, n8_way_1_bit_demultiplexor_1_h;
  wire [15:0] n16_bit_register_1_out_3, n16_bit_register_2_out_3, n16_bit_register_3_out_3,
       n16_bit_register_4_out_3, n16_bit_register_5_out_3, n16_bit_register_6_out_3,
       n16_bit_register_7_out_3, n16_bit_register_8_out_3;

  _8_way_1_bit_Demultiplexor u_8_way_1_bit_demultiplexor_1 (
    .in(load), .a(n8_way_1_bit_demultiplexor_1_a), .b(n8_way_1_bit_demultiplexor_1_b),
    .c(n8_way_1_bit_demultiplexor_1_c), .d(n8_way_1_bit_demultiplexor_1_d),
    .e(n8_way_1_bit_demultiplexor_1_e), .f(n8_way_1_bit_demultiplexor_1_f),
    .g(n8_way_1_bit_demultiplexor_1_g), .h(n8_way_1_bit_demultiplexor_1_h), .sel_2(Address[2]),
    .sel_1(Address[1]), .sel_0(Address[0]));
  _16_bit_Register u_16_bit_register_1 (
    .in_2(In), .out_3(n16_bit_register_1_out_3), .in_1(n8_way_1_bit_demultiplexor_1_a));
  _16_bit_Register u_16_bit_register_2 (
    .in_2(In), .out_3(n16_bit_register_2_out_3), .in_1(n8_way_1_bit_demultiplexor_1_b));
  _16_bit_Register u_16_bit_register_3 (
    .in_2(In), .out_3(n16_bit_register_3_out_3), .in_1(n8_way_1_bit_demultiplexor_1_c));
  _16_bit_Register u_16_bit_register_4 (
    .in_2(In), .out_3(n16_bit_register_4_out_3), .in_1(n8_way_1_bit_demultiplexor_1_d));
  _16_bit_Register u_16_bit_register_5 (
    .in_2(In), .out_3(n16_bit_register_5_out_3), .in_1(n8_way_1_bit_demultiplexor_1_e));
  _16_bit_Register u_16_bit_register_6 (
    .in_2(In), .out_3(n16_bit_register_6_out_3), .in_1(n8_way_1_bit_demultiplexor_1_f));
  _16_bit_Register u_16_bit_register_7 (
    .in_2(In), .out_3(n16_bit_register_7_out_3), .in_1(n8_way_1_bit_demultiplexor_1_g));
  _16_bit_Register u_16_bit_register_8 (
    .in_2(In), .out_3(n16_bit_register_8_out_3), .in_1(n8_way_1_bit_demultiplexor_1_h));
  Clock clock_1 ();  // open: out
  _8_way_16_bit_Multiplexor u_8_way_16_bit_multiplexor_1 (
    .a(n16_bit_register_1_out_3), .b(n16_bit_register_2_out_3), .c(n16_bit_register_3_out_3),
    .d(n16_bit_register_4_out_3), .e(n16_bit_register_5_out_3), .f(n16_bit_register_6_out_3),
    .g(n16_bit_register_7_out_3), .h(n16_bit_register_8_out_3), .out(out), .sel_2(Address[2]),
    .sel_1(Address[1]), .sel_0(Address[0]));

  // Notes on the sheet:
  //   16-Byte RAM
  //   *Contains 8 16-bit Registers
endmodule

module ROM64 (
  input  [5:0] Address,
  output [15:0] out
);

  RAM64 ram64_1 (.In({16{1'b0}}), .Address(Address), .out(out), .load(1'b0));

  // Notes on the sheet:
  //   128-Byte ROM
  //   *Contains 64 16-bit Registers
endmodule
